// Logisim project ALU.circ as structural Verilog: 12 circuits, main circuit main
module main (
  input  [3:0] in_1,
  input  [3:0] in_2,
  input  [5:0] in_3,
  output [3:0] out_4,
  output [3:0] out_5,
  output [3:0] out_6,
  output [3:0] out_7,
  output [3:0] out_8,
  output [3:0] out_9,
  output [3:0] out_10,
  output [3:0] out_11,
  output [3:0] out_12
);

  wire add_sub_en, CLK, feedback_en, undriven;
  wire [3:0] A, B, demux_in_1_a_add_sub, demux_in_1_a_and, demux_in_1_a_neg, demux_in_1_a_or,
       demux_in_1_a_xor, demux_in_1_b_add_sub, demux_in_1_b_and, demux_in_1_b_or, demux_in_1_b_xor,
       demux_in_1_shift, multiplexer_1_out;
  wire [4:0] opcode;

  Clock clock_1 (.out(CLK));
  Multiplexer #(.width(4)) multiplexer_1 (.in0(in_1), .in1(out_5), .out(multiplexer_1_out), .sel(feedback_en));
  Demux_in demux_in_1 (
    .A(A), .B(B), .opcode({feedback_en, opcode[4:3], add_sub_en, opcode[1:0]}), .A_neg(demux_in_1_a_neg),
    .A_xor(demux_in_1_a_xor), .B_xor(demux_in_1_b_xor), .A_or(demux_in_1_a_or), .B_or(demux_in_1_b_or),
    .A_and(demux_in_1_a_and), .B_and(demux_in_1_b_and), .A_add_sub(demux_in_1_a_add_sub),
    .B_add_sub(demux_in_1_b_add_sub), .shift(demux_in_1_shift));
  Register #(.width(4)) register_1 (.D(multiplexer_1_out), .en(undriven), .clk(CLK), .Q(A));  // open: clr
  Register #(.width(4)) register_2 (.D(in_2), .clk(CLK), .Q(B));  // open: en, clr
  Neg neg_1 (.A(demux_in_1_a_neg), .Y(out_4));
  BW_XOR bw_xor_1 (.A(demux_in_1_a_xor), .B(demux_in_1_b_xor), .Y(out_6));
  BW_OR bw_or_1 (.A(demux_in_1_a_or), .B(demux_in_1_b_or), .Y(out_7));
  BW_AND bw_and_1 (.A(demux_in_1_a_and), .B(demux_in_1_b_and), .Y(out_9));
  BW_XOR bw_xor_2 (.A(demux_in_1_b_add_sub), .B({4{opcode[3]}}), .Y(out_11));
  BSR bsr_1 (.A(demux_in_1_shift), .i(opcode[1:0]), .Y(out_12));
  Register #(.width(6)) register_3 (
    .D(in_3), .clk(CLK), .Q({feedback_en, opcode[4:3], add_sub_en, opcode[1:0]}));  // open: en, clr
  Adder_HC adder_hc_1 (.A(demux_in_1_a_add_sub), .B(out_11), .C0(opcode[3]), .Y(out_10));
  Mux_out mux_out_1 (
    .opcode({feedback_en, opcode[4:3], add_sub_en, opcode[1:0]}), .Y_neg(out_4), .Y_xor(out_6), .Y_or(out_7),
    .Y_and(out_9), .Y_add_sub(out_10), .Y_shift(out_12), .Y_out(out_5));
  Register #(.width(4)) register_4 (.D(out_5), .clk(CLK), .Q(out_8));  // open: en, clr

  // Other names for the same wires on the sheet: opcode (some bits) = {feedback_en, add_sub_en}; sub_en = opcode[3];
  //   shift_en = opcode[4]; s1[1:0] = opcode[1:0]; Y_feedback[3:0] = out_5

  // Notes on the sheet:
  //   x00 000 neg
  //   x00 001 xor
  //   x00 010 or
  //   x00 011 and
  //   x00 100 add
  //   x01 100 sub
  //   x10 0xx shift by xx
  //   MSB- feedback enable
endmodule

module Adder_HC (
  input  [3:0] A,
  input  [3:0] B,
  input  C0,
  output [3:0] Y
);

  wire and_1_out, and_2_out, and_3_out, and_4_out, and_5_out, and_6_out, or_1_out, or_2_out, or_3_out,
       xor_1_out, xor_4_out, xor_5_out, xor_7_out;

  xor xor_1 (xor_1_out, B[3], A[3]);
  xor xor_2 (Y[3], xor_1_out, or_1_out);
  and and_1 (and_1_out, B[2], A[2]);
  xor xor_3 (Y[2], xor_4_out, or_2_out);
  xor xor_4 (xor_4_out, B[2], A[2]);
  and and_2 (and_2_out, xor_4_out, or_2_out);
  or or_1 (or_1_out, and_1_out, and_2_out);
  and and_3 (and_3_out, B[1], A[1]);
  xor xor_5 (xor_5_out, B[1], A[1]);
  or or_2 (or_2_out, and_3_out, and_5_out);
  xor xor_6 (Y[1], xor_5_out, or_3_out);
  and and_4 (and_4_out, A[0], xor_7_out);
  and and_5 (and_5_out, xor_5_out, or_3_out);
  xor xor_7 (xor_7_out, B[0], C0);
  or or_3 (or_3_out, and_4_out, and_6_out);
  xor xor_8 (Y[0], xor_7_out, A[0]);
  and and_6 (and_6_out, B[0], C0);

  // Notes on the sheet:
  //   P3
  //   G2
  //   P2
  //   G2:0
  //   G1
  //   P1
  //   G0
  //   G1:0
  //   G0:0
endmodule

module BW_NOT (
  input  [3:0] A,
  output [3:0] Y
);

  not not_1 (Y[0], A[0]);
  not not_2 (Y[1], A[1]);
  not not_3 (Y[2], A[2]);
  not not_4 (Y[3], A[3]);
endmodule

module BW_OR (
  input  [3:0] A,
  input  [3:0] B,
  output [3:0] Y
);

  or or_1 (Y[0], A[0], B[0]);
  or or_2 (Y[1], A[1], B[1]);
  or or_3 (Y[2], A[2], B[2]);
  or or_4 (Y[3], A[3], B[3]);
endmodule

module BW_AND (
  input  [3:0] A,
  input  [3:0] B,
  output [3:0] Y
);

  and and_1 (Y[0], A[0], B[0]);
  and and_2 (Y[1], A[1], B[1]);
  and and_3 (Y[2], A[2], B[2]);
  and and_4 (Y[3], A[3], B[3]);
endmodule

module BW_XOR (
  input  [3:0] A,
  input  [3:0] B,
  output [3:0] Y
);

  xor xor_1 (Y[0], A[0], B[0]);
  xor xor_2 (Y[1], A[1], B[1]);
  xor xor_3 (Y[2], A[2], B[2]);
  xor xor_4 (Y[3], A[3], B[3]);
endmodule

module BSR (
  input  [3:0] A,
  input  [1:0] i,
  output [3:0] Y
);

  wire multiplexer_1_out, multiplexer_2_out, multiplexer_3_out, multiplexer_4_out;

  Multiplexer multiplexer_1 (.in0(A[0]), .in1(A[2]), .out(multiplexer_1_out), .sel(i[1]));
  Multiplexer multiplexer_2 (.in0(A[1]), .in1(A[3]), .out(multiplexer_2_out), .sel(i[1]));
  Multiplexer multiplexer_3 (.in0(A[2]), .in1(A[0]), .out(multiplexer_3_out), .sel(i[1]));
  Multiplexer multiplexer_4 (.in0(A[3]), .in1(A[1]), .out(multiplexer_4_out), .sel(i[1]));
  Multiplexer multiplexer_5 (.in0(multiplexer_1_out), .in1(multiplexer_2_out), .out(Y[0]), .sel(i[0]));
  Multiplexer multiplexer_6 (.in0(multiplexer_2_out), .in1(multiplexer_3_out), .out(Y[1]), .sel(i[0]));
  Multiplexer multiplexer_7 (.in0(multiplexer_3_out), .in1(multiplexer_4_out), .out(Y[2]), .sel(i[0]));
  Multiplexer multiplexer_8 (.in0(multiplexer_4_out), .in1(multiplexer_1_out), .out(Y[3]), .sel(i[0]));

  // Other names for the same wires on the sheet: K0 = i[0]; K1 = i[1]
endmodule

module Neg (
  input  [3:0] A,
  output [3:0] Y
);

  wire or_1_out, or_2_out;

  or or_1 (or_1_out, A[0], A[1]);
  or or_2 (or_2_out, or_1_out, A[2]);
  xor xor_1 (Y[1], A[0], A[1]);
  xor xor_2 (Y[2], or_1_out, A[2]);
  xor xor_3 (Y[3], or_2_out, A[3]);

  assign Y[0] = A[0];
endmodule

module Demux_in (
  input  [3:0] A,
  input  [3:0] B,
  input  [5:0] opcode,
  output [3:0] A_neg,
  output [3:0] A_xor,
  output [3:0] B_xor,
  output [3:0] A_or,
  output [3:0] B_or,
  output [3:0] A_and,
  output [3:0] B_and,
  output [3:0] A_add_sub,
  output [3:0] B_add_sub,
  output [3:0] shift
);

  wire [3:0] demultiplexer_1_out0, demultiplexer_2_out0, demultiplexer_3_out0, demultiplexer_5_out0;

  Demultiplexer #(.width(4)) demultiplexer_1 (.out0(demultiplexer_1_out0), .out1(shift), .in(A), .sel(opcode[4]));
  Demultiplexer #(.width(4)) demultiplexer_2 (.out0(demultiplexer_2_out0), .out1(B_add_sub), .in(B), .sel(opcode[2]));
  Demultiplexer #(.width(4)) demultiplexer_3 (
    .out0(demultiplexer_3_out0), .out1(A_add_sub), .in(demultiplexer_1_out0), .sel(opcode[2]));
  Demultiplexer #(.select(2), .width(4)) demultiplexer_4 (
    .out0(A_neg), .out1(A_xor), .out2(A_or), .out3(A_and), .in(demultiplexer_3_out0), .sel(opcode[1:0]));
  Demultiplexer #(.select(2), .width(4)) demultiplexer_5 (
    .out0(demultiplexer_5_out0), .out1(B_xor), .out2(B_or), .out3(B_and), .in(demultiplexer_2_out0),
    .sel(opcode[1:0]));
  // NoConnect on demultiplexer_5_out0

  // Other names for the same wires on the sheet: A_bw_and[3:0] = A_and; A_bw_or[3:0] = A_or; A_bw_xor[3:0] = A_xor;
  //   B_bw_and[3:0] = B_and; B_bw_or[3:0] = B_or; B_bw_xor[3:0] = B_xor; add_sub_en = opcode[2]; sub_en = opcode[3];
  //   shift_en = opcode[4]; feedback_en = opcode[5]; s1[1:0] = opcode[1:0]
endmodule

module Mux_out (
  input  [5:0] opcode,
  input  [3:0] Y_neg,
  input  [3:0] Y_xor,
  input  [3:0] Y_or,
  input  [3:0] Y_and,
  input  [3:0] Y_add_sub,
  input  [3:0] Y_shift,
  output [3:0] Y_out
);

  wire [3:0] multiplexer_1_out, multiplexer_2_out;

  Multiplexer #(.select(2), .width(4)) multiplexer_1 (
    .in0(Y_neg), .in1(Y_xor), .in2(Y_or), .in3(Y_and), .out(multiplexer_1_out), .sel(opcode[1:0]));
  Multiplexer #(.width(4)) multiplexer_2 (
    .in0(multiplexer_1_out), .in1(Y_add_sub), .out(multiplexer_2_out), .sel(opcode[2]));
  Multiplexer #(.width(4)) multiplexer_3 (.in0(multiplexer_2_out), .in1(Y_shift), .out(Y_out), .sel(opcode[4]));

  // Other names for the same wires on the sheet: add_sub_en = opcode[2]; sub_en = opcode[3]; shift_en = opcode[4];
  //   feedback_en = opcode[5]; s1[1:0] = opcode[1:0]; Y[3:0] = Y_out
endmodule

module demux_4bits (
  input  [3:0] A,
  input  s,
  output [3:0] out0,
  output [3:0] out1
);

  wire not_1_out;

  not not_1 (not_1_out, s);
  and and_1 (out0[0], not_1_out, A[0]);
  and and_2 (out1[0], A[0], s);
  and and_3 (out0[1], not_1_out, A[1]);
  and and_4 (out1[1], A[1], s);
  and and_5 (out0[2], not_1_out, A[2]);
  and and_6 (out1[2], A[2], s);
  and and_7 (out0[3], not_1_out, A[3]);
  and and_8 (out1[3], A[3], s);

  // Other names for the same wires on the sheet: out_0[3:0] = out0; out_1[3:0] = out1
endmodule

module demux_4bits_bigger (
  input  [3:0] A,
  input  [1:0] s,
  output [3:0] out0,
  output [3:0] out1,
  output [3:0] out2,
  output [3:0] out3
);

  wire [3:0] demux_4bits_1_out0, demux_4bits_1_out1;

  demux_4bits demux_4bits_1 (.A(A), .s(s[1]), .out0(demux_4bits_1_out0), .out1(demux_4bits_1_out1));
  demux_4bits demux_4bits_2 (.A(demux_4bits_1_out0), .s(s[0]), .out0(out0), .out1(out1));
  demux_4bits demux_4bits_3 (.A(demux_4bits_1_out1), .s(s[0]), .out0(out2), .out1(out3));

  // Other names for the same wires on the sheet: out_0[3:0] = out0; out_1[3:0] = out1; out_2[3:0] = out2;
  //   out_3[3:0] = out3
endmodule
